# Fritzing sketch ASMO_wiring (saved by Fritzing 0.9.3b)
perfboards: 3

parts:
  Raspberry_Pi2 = Raspberry Pi B+  # not connected
  Part1 = KY-005 Infrared Transmitter Module [package="Breakout board"]
  Part5 = KY-009 Full Color RGB LED SMD Module [package="Breakout board"]
  Part3 = KY-015 Temperature & Humidity Sensor Module [package="Breakout board"]
  Part4 = KY-022 Infrared Receiver Module [package="Breakout board"]
  hc-sr1 = hc-sr04
  R2 = Resistor [tolerance=±5% resistance=2.2k package="0805 [SMD]"]
  R1 = Resistor [tolerance=±5% resistance=1k package="0805 [SMD]"]
  J1 = Basic Servo
  Bauteil1 = Adafruit Pi Cobbler Plus [part_number="Adafruit #2029"]
  hc-sr2 = hc-sr04  # not connected
  R3 = Resistor [tolerance=±5% resistance=1k package="0805 [SMD]"]  # not connected
  R4 = Resistor [tolerance=±5% resistance=2.2k package="0805 [SMD]"]  # not connected

nets:
  N1: Part1.Vin, Bauteil1.GPIO16
  GND: Part1.-, Part5.-, Part3.-, Part4.-, hc-sr1.GND, R2.Pin_0, J1.gnd, Bauteil1.GND
  N2: Part5.R, Bauteil1.GPIO26
  N3: Part5.G, Bauteil1.GPIO19
  N4: Part5.B, Bauteil1.GPIO13
  N5: Part3.S, Bauteil1.GPIO4
  VIN: Part3.Vin, Part4.Vin, Bauteil1.+3.3V
  N6: Part4.S, Bauteil1.GPIO25
  VCC: hc-sr1.VCC, J1.vcc, Bauteil1.+5V
  N7: hc-sr1.Trig, Bauteil1.GPIO21
  N8: hc-sr1.Echo, R1.Pin_0
  N9: R2.Pin_1, R1.Pin_1, Bauteil1.GPIO20
  N10: J1.pulse, Bauteil1.GPIO12

notes:
  3 Color RGB LED:
  Please note R and G are switched in the real Circuit (wiring is correct though in regards of the order)

custom parts:
  KY-005 Infrared Transmitter Module: Arduino IR Transmitter Module Keyes KY-005, emits infrared light at 38KHz.
  KY-009 Full Color RGB LED SMD Module: RGB full color LED Module KY-009 for Arduino, emits a range of colors by mixing red, green and blue. The amount of each primary color is adjusted using PWM.
  KY-015 Temperature & Humidity Sensor Module: KY-015 temperature and humidity sensor module, provides a low-latency serial interface to measure humidity and temperature.
  KY-022 Infrared Receiver Module: Arduino IR receiver module KY-022, reacts to 38kHz infrared light.
  Adafruit Pi Cobbler Plus: The Raspberry Pi B+/Pi 2/ Pi 3 has landed on the Maker World like a 40-GPIO pinned, quad-USB ported, credit card sized bomb of DIY joy. And while you can use most of our great Model B accessories by hooking up our downgrade cable, its probably a good time to upgrade your set up and accessorize using all of the Model B+'s / Pi 2's / Pi 3's 40 pins. That's why we now carry the Adafruit Assembled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
